# Fritzing sketch ejercicio_1 (saved by Fritzing 0.9.3b)
breadboards: 1

parts:
  Cerebro = Arduino Uno (Rev3) - ICSP
  LCD = LCD screen
  R1 = Rotary Potentiometer (Large) [maximum_resistance=100kΩ package=THT]
  DHT2 = Humidity and Temperature Sensor DHT11

nets (from the schematic view):
  5V: Cerebro.5V, LCD.VDD, LCD.LED+, R1.leg2, DHT2.Vcc
  N1: Cerebro.D8, LCD.DB4
  N2: Cerebro.D9_PWM, LCD.DB5
  N3: Cerebro.D10_PWM/SS, LCD.DB6
  N4: Cerebro.D11_PWM/MOSI, LCD.DB7
  N5: Cerebro.D12/MISO, DHT2.Data-signal
  N6: Cerebro.D2, LCD.RS
  N7: Cerebro.D4, LCD.E
  GND: Cerebro.GND, LCD.VSS, LCD.R/W, LCD.LED-, R1.leg1, DHT2.GND_2
  N8: LCD.V0, R1.wiper

custom parts:
  Humidity and Temperature Sensor DHT11: Digital relative humidity & temperature sensor DHT11
